# Fritzing sketch HockeyBar (saved by Fritzing 0.9.4)
breadboards: 1

parts:
  LED1 = 7-SEGMENT-4DIGIT-TM1637
  8x8_LED_Modul_mit_MAX1 = 8x8 LED Modul mit MAX7219 [package=THT]
  8x8_LED_Modul_mit_MAX2 = 8x8 LED Modul mit MAX7219 [package=THT]
  8x8_LED_Modul_mit_MAX3 = 8x8 LED Modul mit MAX7219 [package=THT]
  8x8_LED_Modul_mit_MAX4 = 8x8 LED Modul mit MAX7219 [package=THT]
  Raspberry_Pi_B_rev1 = Raspberry Pi B rev1
  8x8_LED_Modul_mit_MAX5 = 8x8 LED Modul mit MAX7219 [package=THT]
  IRR1 = IR reciver [chip_label=RE package="DIP (Dual Inline) [THT]"]
  IRE1 = IR emitter [chip_label=EM package="DIP (Dual Inline) [THT]"]
  IRR2 = IR reciver [chip_label=RE package="DIP (Dual Inline) [THT]"]
  IRE2 = IR emitter [chip_label=EM package="DIP (Dual Inline) [THT]"]
  IRR3 = IR reciver [chip_label=RE package="DIP (Dual Inline) [THT]"]
  IRE3 = IR emitter [chip_label=EM package="DIP (Dual Inline) [THT]"]
  IRR4 = IR reciver [chip_label=RE package="DIP (Dual Inline) [THT]"]
  IRE4 = IR emitter [chip_label=EM package="DIP (Dual Inline) [THT]"]
  IRR5 = IR reciver [chip_label=RE package="DIP (Dual Inline) [THT]"]
  IRE5 = IR emitter [chip_label=EM package="DIP (Dual Inline) [THT]"]

nets:
  N1: LED1.CLK-IN, Raspberry_Pi_B_rev1.GPIO_1
  N2: LED1.DIO-IN, Raspberry_Pi_B_rev1.GPIO_0
  N3: 8x8_LED_Modul_mit_MAX1.VCC_Eingang, 8x8_LED_Modul_mit_MAX3.VCC_Ausgang
  N4: 8x8_LED_Modul_mit_MAX1.GND_Eingang, 8x8_LED_Modul_mit_MAX3.GND_Ausgang
  N5: 8x8_LED_Modul_mit_MAX1.DIN_Eingang, 8x8_LED_Modul_mit_MAX3.DOUT_Ausgang
  N6: 8x8_LED_Modul_mit_MAX1.CS_Eingang, 8x8_LED_Modul_mit_MAX3.CS_Ausgang
  N7: 8x8_LED_Modul_mit_MAX1.CLK_Eingang, 8x8_LED_Modul_mit_MAX3.CLK_Ausgang
  N8: 8x8_LED_Modul_mit_MAX1.VCC_Ausgang, 8x8_LED_Modul_mit_MAX2.VCC_Eingang
  N9: 8x8_LED_Modul_mit_MAX1.GND_Ausgang, 8x8_LED_Modul_mit_MAX2.GND_Eingang
  N10: 8x8_LED_Modul_mit_MAX1.DOUT_Ausgang, 8x8_LED_Modul_mit_MAX2.DIN_Eingang
  N11: 8x8_LED_Modul_mit_MAX1.CS_Ausgang, 8x8_LED_Modul_mit_MAX2.CS_Eingang
  N12: 8x8_LED_Modul_mit_MAX1.CLK_Ausgang, 8x8_LED_Modul_mit_MAX2.CLK_Eingang
  N13: 8x8_LED_Modul_mit_MAX2.VCC_Ausgang, 8x8_LED_Modul_mit_MAX5.VCC_Eingang
  N14: 8x8_LED_Modul_mit_MAX2.GND_Ausgang, 8x8_LED_Modul_mit_MAX5.GND_Eingang
  N15: 8x8_LED_Modul_mit_MAX2.DOUT_Ausgang, 8x8_LED_Modul_mit_MAX5.DIN_Eingang
  N16: 8x8_LED_Modul_mit_MAX2.CS_Ausgang, 8x8_LED_Modul_mit_MAX5.CS_Eingang
  N17: 8x8_LED_Modul_mit_MAX2.CLK_Ausgang, 8x8_LED_Modul_mit_MAX5.CLK_Eingang
  N18: 8x8_LED_Modul_mit_MAX3.VCC_Eingang, 8x8_LED_Modul_mit_MAX4.VCC_Ausgang
  N19: 8x8_LED_Modul_mit_MAX3.GND_Eingang, 8x8_LED_Modul_mit_MAX4.GND_Ausgang
  N20: 8x8_LED_Modul_mit_MAX3.DIN_Eingang, 8x8_LED_Modul_mit_MAX4.DOUT_Ausgang
  N21: 8x8_LED_Modul_mit_MAX3.CS_Eingang, 8x8_LED_Modul_mit_MAX4.CS_Ausgang
  N22: 8x8_LED_Modul_mit_MAX3.CLK_Eingang, 8x8_LED_Modul_mit_MAX4.CLK_Ausgang
  5V: 8x8_LED_Modul_mit_MAX4.VCC_Eingang, Raspberry_Pi_B_rev1.5V, IRR1.5V, IRE1.5V, IRR2.5V, IRE2.5V, IRR3.5V, IRE3.5V, IRR4.5V, IRE4.5V, IRR5.5V, IRE5.5V
  GND: 8x8_LED_Modul_mit_MAX4.GND_Eingang, Raspberry_Pi_B_rev1.GND, IRR1.GND, IRE1.GND, IRR2.GND, IRE2.GND, IRR3.GND, IRE3.GND, IRR4.GND, IRE4.GND, IRR5.GND, IRE5.GND
  N23: 8x8_LED_Modul_mit_MAX4.DIN_Eingang, Raspberry_Pi_B_rev1.GPIO_10
  N24: 8x8_LED_Modul_mit_MAX4.CS_Eingang, Raspberry_Pi_B_rev1.GPIO_8
  N25: 8x8_LED_Modul_mit_MAX4.CLK_Eingang, Raspberry_Pi_B_rev1.GPIO_11
  N26: Raspberry_Pi_B_rev1.GPIO_23, IRR2.SIG
  N27: Raspberry_Pi_B_rev1.GPIO_17, IRR4.SIG
  N28: Raspberry_Pi_B_rev1.GPIO_21, IRR1.SIG
  N29: Raspberry_Pi_B_rev1.GPIO_22, IRR5.SIG
  N30: Raspberry_Pi_B_rev1.GPIO_24, IRR3.SIG
